# Fritzing sketch GripperSketch (saved by Fritzing 0.8.7b)
breadboards: 1

parts:
  Part1 = Arduino Nano (Rev3.0)
  L298 = L298N DC motor driver
  Gripper_motor = Stepper Motor - Bipolar
  "EStop" = Toggle Switch [package=THT]
  LM2596_(24v_to_5v) = LM2596 step down module
  24v_input_--> = mystery part, 3 pins [chip_label=?]
  PC817_-_Open|Close_(input) = Sharp PC817 [package=THT]
  Hit_sensor = Toggle Switch [package=THT]
  Acknowledge_(output) = RELAY [package=relay-jzc]
  Hold/EStop_(output) = RELAY [package=relay-jzc]
  Raspberry_Pi_B_rev1 = Raspberry Pi B rev2
  LM2596_(24v_to_5v)_2 = LM2596 step down module
  Test_button_(Optional) = Round Pushbutton
  Part2 = SRF05 Ultrasonic Rangefinder

nets:
  GND: Part1.GND, L298.GND, "EStop".COM, LM2596_(24v_to_5v).IN-, LM2596_(24v_to_5v).OUT-, 24v_input_-->.pin1, PC817_-_Open|Close_(input).Pin_2, Hit_sensor.COM, Acknowledge_(output).NC, Hold/EStop_(output).NC, Part2.GND
  N1: Part1.D2, L298.IN1
  N2: Part1.D3, L298.IN2
  N3: Part1.D4, L298.IN3
  N4: Part1.D5, L298.IN4
  N5: Part1.D6, "EStop".L2
  N6: Part1.D7, PC817_-_Open|Close_(input).Pin_1
  N7: Part1.D8, Hold/EStop_(output).NO
  N8: Part1.D9, Acknowledge_(output).NO
  N9: Part1.D10, Hit_sensor.L2
  N10: Part1.D11/MOSI, Part2.Trig
  N11: Part1.D12/MISO, Part2.Echo
  VIN: Part1.VIN, L298.12V, LM2596_(24v_to_5v).OUT+, Acknowledge_(output).COIL2, Hold/EStop_(output).COIL2, Part2.VCC
  N12: Part1.A5, Raspberry_Pi_B_rev1.GPIO_3
  N13: Part1.A4, Raspberry_Pi_B_rev1.GPIO_2
  N14: L298.OUT1, Gripper_motor.C
  N15: L298.OUT2, Gripper_motor.A
  N16: L298.OUT3, Gripper_motor.B
  N17: L298.OUT4, Gripper_motor.D
  N18: LM2596_(24v_to_5v).IN+, 24v_input_-->.pin3
  N19: PC817_-_Open|Close_(input).Pin_4, Test_button_(Optional).leg1
  N20: LM2596_(24v_to_5v)_2.IN-, LM2596_(24v_to_5v)_2.OUT-

custom parts:
  L298N DC motor driver: 2x DC motor driver with 78M05 positive voltage regulator (7..35 V) L298N: max 46 V, 2 A Set 5 V Enable jumper to enable 5 V regultor (needed for the L298N) and +5 V output at screw terminal or supply external +5 V at screw terminal Set ENA and/or ENB to +5 V to enable motor permanently or supply ENA and/or ENB with PWM signal IN1 and IN2 set rotation directory for motor A (OUT1/OUT2) IN2 and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
  LM2596 step down module: LM2596 DC-DC step down power supply module 3 A.
